# Fritzing sketch button_nano (saved by Fritzing 1.0.1rc)
breadboards: 1

parts:
  Part2 = Arduino Nano (Rev3.0)
  S2 = Pushbutton [package="[THT]"]
  LED3 = LED - 3mm [color="Red (633nm)" current=0.030A package="3 mm [THT]"]
  R3 = Resistor [tolerance=±5% power=0.25W resistance=1000 package=THT]
  R4 = Resistor [tolerance=±5% power=0.25W resistance=1000 package=THT]
  R5 = Resistor [tolerance=±5% power=0.25W resistance=1000 package=THT]
  VCC1 = Battery block 9V

nets:
  N1: Part2.GND, LED3.cathode, R4.Pin_1, VCC1.-
  N2: Part2.D7, R4.Pin_0, R5.Pin_0
  N3: Part2.D11/MOSI, R3.Pin_1
  N4: Part2.VIN, VCC1.+
  N5: Part2.5V, S2.Pin_1, S2.Pin_2
  N6: S2.Pin_3, S2.Pin_4, R5.Pin_1
  N7: LED3.anode, R3.Pin_0
