# Fritzing sketch led_basic_nano (saved by Fritzing 1.0.1rc)
breadboards: 1

parts:
  VCC3 = Battery block 9V
  Part4 = Arduino Nano (Rev3.0)
  R4 = Resistor [tolerance=±5% power=0.25W resistance=1k package=THT]
  LED4 = smd LED [color="Red (633nm)" package="0603 [SMD]"]

nets:
  N1: VCC3.-, Part4.GND, LED4.cathode
  N2: VCC3.+, Part4.VIN
  N3: Part4.D3, R4.Pin_0
  N4: R4.Pin_1, LED4.anode
