# Fritzing sketch led_switch_nano (saved by Fritzing 1.0.1rc)
breadboards: 1

parts:
  Part2 = Arduino Nano (Rev3.0)
  LED3 = LED - 3mm [color="Red (633nm)" current=0.030A package="3 mm [THT]"]
  R3 = Resistor [tolerance=±5% power=0.25W resistance=1000 package=THT]
  VCC1 = Battery block 9V
  U1 = SWITCH_SPDT [package=kps-1290]

nets:
  N1: Part2.GND, LED3.cathode, VCC1.-, U1.O
  N2: Part2.D2, U1.P
  N3: Part2.D8, R3.Pin_1
  N4: Part2.VIN, VCC1.+
  N5: Part2.5V, U1.S
  N6: LED3.anode, R3.Pin_0
