# Fritzing sketch motor_nano (saved by Fritzing 1.0.1rc)
breadboards: 1

parts:
  M1 = DC Motor [voltage_(max)=6V voltage_(min)=3V]
  Part3 = Arduino Nano (Rev3.0)
  VCC2 = Battery block 9V

nets:
  N1: M1.pin_1, Part3.D9
  N2: M1.pin_2, Part3.GND, VCC2.-
  N3: Part3.VIN, VCC2.+

notes:
  The motor does not matter which way it goes. What happens when you reverse the wires?
