# Fritzing sketch photoresistor_nano (saved by Fritzing 1.0.1rc)
breadboards: 1

parts:
  Part1 = Arduino Nano (Rev3.0)
  LED1 = LED - 3mm [color="Red (633nm)" current=0.030A package="3 mm [THT]"]
  R1 = Resistor [tolerance=±5% power=0.25W resistance=1000 package=THT]  # not connected
  R2 = Resistor [tolerance=±5% power=0.25W resistance=15k package=THT]
  R6 = PHOTOCELL [package=photocell-kit]
  VCC4 = Battery block 9V

nets:
  N1: Part1.GND, LED1.anode, R6.P$2, VCC4.-
  N2: Part1.VIN, VCC4.+
  N3: Part1.A7, R2.Pin_0
  N4: Part1.A1, R2.Pin_1, R6.P$1
