# Fritzing sketch potent_nano (saved by Fritzing 1.0.1rc)
breadboards: 1

parts:
  R1 = TRIMPOT [maximum_resistance=10kΩ knob_status=50% power=0.5W package=trim_pot_pth]
  LED7 = smd LED [color="Red (633nm)" package="0603 [SMD]"]
  R1_2 = Resistor [tolerance=±5% power=0.25W resistance=1k package=THT]
  Part2 = Arduino Nano (Rev3.0)
  VCC4 = Battery block 9V

nets:
  N1: R1.CCW, LED7.cathode, Part2.GND, VCC4.-
  N2: R1.WIPER, Part2.A0
  N3: R1.CW, Part2.5V
  N4: LED7.anode, R1_2.Pin_1
  N5: R1_2.Pin_0, Part2.D10
  N6: Part2.VIN, VCC4.+
